# Fritzing sketch schem (saved by Fritzing 0.8.7b)

parts:
  Part1 = Arduino Uno (Rev3)
  1/REc = Square Pushbutton
  Part2 = NeoPixel Stick [part_number=1426]
  U2 = MIDI_CONN_FEMALE [package=din_5_female]
  TRS1 = Audio Jack (TRS) 3.5mm [package="PG203J [THT]"]
  PG_DN = Square Pushbutton
  PG_UP = Square Pushbutton
  TUNER = Square Pushbutton
  2/PLAY = Square Pushbutton
  3/STOP = Square Pushbutton
  MODE = Square Pushbutton
  4/EMPTY = Square Pushbutton
  TRS2 = Stereo Jack (TRS) 3.5mm [package="PG203J [THT]"]
  R1 = Resistor [tolerance=±5% resistance=220 package=THT]
  R2 = Resistor [tolerance=±5% resistance=220 package=THT]
  R3 = Resistor [tolerance=±5% resistance=100k package=THT]
  R4 = Resistor [tolerance=±5% resistance=100k package=THT]

nets:
  N1: Part1.A0, TRS1.Tip, R3.Pin_1
  N2: Part1.A1, TRS2.Tip, R4.Pin_1
  N3: Part1.D8, PG_DN.leg0
  N4: Part1.D9_PWM, TUNER.leg0
  N5: Part1.D10_PWM/SS, PG_UP.leg0
  N6: Part1.D11_PWM/MOSI, MODE.leg0
  GND: Part1.GND, 1/REc.leg1, Part2.GND, U2.NC1, TRS1.Sleeve, PG_DN.leg1, PG_UP.leg1, TUNER.leg1, 2/PLAY.leg1, 3/STOP.leg1, MODE.leg1, 4/EMPTY.leg1, TRS2.Sleeve, R3.Pin_0, R4.Pin_0
  N7: Part1.D1/TX, R1.Pin_1
  N8: Part1.D2, 1/REc.leg0
  N9: Part1.D3_PWM, 2/PLAY.leg0
  N10: Part1.D4, 3/STOP.leg0
  N11: Part1.D5_PWM, 4/EMPTY.leg0
  N12: Part1.D6_PWM, Part2.DATAIN
  5V: Part1.5V, Part2.+5V, TRS1.Ring, TRS2.Ring, R2.Pin_1
  N13: U2.MIDI_IN, R1.Pin_0
  N14: U2.MIDI_OUT, R2.Pin_0

custom parts:
  NeoPixel Stick: Make your own little LED strip arrangement with this stick of NeoPixel LEDs. We crammed 8 of the tiny 5050 (5mm x 5mm) smart RGB LEDs onto a PCB with mounting holes and a chainable design. Use only one microcontroller pin to control as many as you can chain together! Each LED is addressable as the driver chip is inside the LED. Each one has ~18mA constant current drive so the color will be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
